// Logisim project N1_Processador_MIPS.circ as structural Verilog: 2 circuits, main circuit main
module main (
  input  in_1,
  output [7:0] out_2
);

  wire clock_1_out;
  wire [7:0] adder_1_out, PC_q;

  Clock clock_1 (.out(clock_1_out));
  Register PC (.D(adder_1_out), .Q(PC_q), .clk(clock_1_out), .clr(in_1));  // open: en
  Adder adder_1 (.a(8'h1), .b(PC_q), .out(adder_1_out));  // open: cin, cout
  ROM rom_1 (.addr(PC_q), .data(out_2));  // open: sel
  Banco_de_Registradores banco_de_registradores_1 ();  // open: Read_Register_1, Read_Register_2, Write_Data, Reg_Write, Write_Register, CLOCK, CLEAR, Read_Data_1, Read_Data_2

  // Notes on the sheet:
  //   contents of rom_1 (hex, n*v repeats v):
  //   1 ff 2 6
endmodule

module Banco_de_Registradores (
  input  [2:0] Read_Register_1,
  input  [2:0] Read_Register_2,
  input  [7:0] Write_Data,
  input  Reg_Write,
  input  [2:0] Write_Register,
  input  CLOCK,
  input  CLEAR,
  output [7:0] Read_Data_1,
  output [7:0] Read_Data_2
);

  wire Enable0, Enable1, Enable2, Enable3, Enable4, Enable5, Enable6, Enable7;
  wire [7:0] Reg0, Reg1, Reg2, Reg3, Reg4, Reg5, Reg6, Reg7, WReg0, WReg1, WReg2, WReg3, WReg4, WReg5, WReg6,
       WReg7;

  Demultiplexer #(.select(3), .width(8)) demultiplexer_1 (
    .out0(WReg0), .out1(WReg1), .out2(WReg2), .out3(WReg3), .out4(WReg4), .out5(WReg5), .out6(WReg6),
    .out7(WReg7), .in(Write_Data), .sel(Write_Register));  // open: en
  Demultiplexer #(.select(3)) demultiplexer_2 (
    .out0(Enable0), .out1(Enable1), .out2(Enable2), .out3(Enable3), .out4(Enable4), .out5(Enable5),
    .out6(Enable6), .out7(Enable7), .in(Reg_Write), .sel(Write_Register));  // open: en
  Register u_Reg0 (.D(WReg0), .en(Enable0), .Q(Reg0), .clk(CLOCK), .clr(CLEAR));
  Register u_Reg1 (.D(WReg1), .en(Enable1), .Q(Reg1), .clk(CLOCK), .clr(CLEAR));
  Register u_Reg2 (.D(WReg2), .en(Enable2), .Q(Reg2), .clk(CLOCK), .clr(CLEAR));
  Register u_Reg3 (.D(WReg3), .en(Enable3), .Q(Reg3), .clk(CLOCK), .clr(CLEAR));
  Register u_Reg4 (.D(WReg4), .en(Enable4), .Q(Reg4), .clk(CLOCK), .clr(CLEAR));
  Register u_Reg5 (.D(WReg5), .en(Enable5), .Q(Reg5), .clk(CLOCK), .clr(CLEAR));
  Register u_Reg6 (.D(WReg6), .en(Enable6), .Q(Reg6), .clk(CLOCK), .clr(CLEAR));
  Register u_Reg7 (.D(WReg7), .en(Enable7), .Q(Reg7), .clk(CLOCK), .clr(CLEAR));
  Multiplexer #(.select(3), .width(8)) multiplexer_1 (
    .in0(Reg0), .in1(Reg1), .in2(Reg2), .in3(Reg3), .in4(Reg4), .in5(Reg5), .in6(Reg6), .in7(Reg7),
    .out(Read_Data_1), .sel(Read_Register_1));  // open: en
  Multiplexer #(.select(3), .width(8)) multiplexer_2 (
    .in0(Reg0), .in1(Reg1), .in2(Reg2), .in3(Reg3), .in4(Reg4), .in5(Reg5), .in6(Reg6), .in7(Reg7),
    .out(Read_Data_2), .sel(Read_Register_2));  // open: en

  // Other names for the same wires on the sheet: Read_Reg1[2:0] = Read_Register_1; Read_Reg2[2:0] = Read_Register_2
endmodule
